# Fritzing sketch Schematic (saved by Fritzing 0.9.3b)
breadboards: 1

parts:
  Part1 = Arduino Uno (Rev3)
  LED1 = LED - 5mm [color="Red (633nm)" package="5 mm [THT]"]
  R1 = Resistor [tolerance=±5% resistance=220 package=THT]
  S1 = Pushbutton [package="[THT]"]

nets:
  N1: Part1.D7, R1.Pin_0, S1.Pin_1, S1.Pin_2
  N2: Part1.5V, S1.Pin_3, S1.Pin_4
  N3: LED1.cathode, R1.Pin_1
